# Fritzing sketch Ubidots-DHT22-Pi-Connections (saved by Fritzing 0.9.2b)
breadboards: 1

parts:
  Raspberry_Pi1 = Raspberry Pi B+
  DHT2 = DHT22 Humidity and Temperature Sensor
  R1 = Resistor [tolerance=±20% resistance=10k package=THT]

nets:
  3V3: Raspberry_Pi1.3v3, DHT2.VDD, R1.Pin_0
  N1: Raspberry_Pi1.GPIO4, DHT2.DATA, R1.Pin_1
  GND: Raspberry_Pi1.GND, DHT2.GND
